# Fritzing sketch Lab 4 Circuit (saved by Fritzing 0.9.3b)
breadboards: 1

parts:
  Part1 = Arduino Due (Rev2b)
  R1 = Photocell (LDR) [package=THT]
  R2 = Photocell (LDR) [package=THT]

nets:
  N1: Part1.A0, R2.pin_0
  N2: Part1.A7, R1.pin_0
  N3: Part1.IOREF, R1.pin_1, R2.pin_1
