# Fritzing sketch Lab 3 Circuit 1 (saved by Fritzing 0.9.3b)
breadboards: 1

parts:
  Q1 = NPN-Transistor [package="TO92 [THT]"]
  M1 = DC Motor
  Part1 = Arduino Due (Rev2b)

nets:
  N1: Q1.E, Part1.GND
  N2: Q1.B, M1.pin_2
  N3: Q1.C, Part1.D7_PWM
