# Fritzing sketch lab 3  (saved by Fritzing 0.9.3b)
breadboards: 1

parts:
  Part1 = Arduino Uno (Rev3)
  R1 = Resistor [tolerance=±5% resistance=220 package=THT]
  Q1 = NPN-Transistor [package="TO92 [THT]"]
  Q2 = NPN-Transistor [package="TO92 [THT]"]
  R2 = Resistor [tolerance=±5% resistance=220 package=THT]
  M1 = DC Motor
  U1 = LIPO-2000mAh [package=lipo-2000]

nets:
  N1: Part1.GND, R1.Pin_0, Q1.C, Q2.E, U1.-
  N2: Part1.3V3, R2.Pin_1
  N3: R1.Pin_1, Q1.E
  N4: Q1.B, Q2.C, R2.Pin_0
  N5: Q2.B, M1.pin_1
  N6: M1.pin_2, U1.+
